// Logisim project control-logic.circ as structural Verilog: 1 circuit, main circuit control_logic
module control_logic (
  input  [31:0] inst,
  input  BrEq,
  input  BrLt,
  output PCSel,
  output RegWEn,
  output [2:0] ImmSel,
  output BrUn,
  output ASel,
  output BSel,
  output [3:0] ALUSel,
  output MemRW,
  output [1:0] WBSel,
  output CSRSel,
  output CSRWen
);

  wire comparator_2_eq, comparator_3_eq, comparator_4_eq, comparator_5_eq, comparator_6_eq, comparator_7_eq,
       comparator_8_eq, comparator_9_eq, is_addi, is_andi, is_i_type, is_ori, is_slli, is_slti, is_srai,
       is_srli, is_xori;
  wire [4:0] priority_encoder_1_out;
  wire [5:0] bit_extender_1_out;
  wire [15:0] rom_1_data;

  Comparator #(.width(7)) comparator_1 (.a(inst[6:0]), .b(7'b1111011), .eq(is_i_type));  // open: gt, lt
  Comparator #(.width(3)) comparator_2 (.a(inst[14:12]), .b(3'b000), .eq(comparator_2_eq));  // open: gt, lt
  Comparator #(.width(3)) comparator_3 (.a(inst[14:12]), .b(3'b001), .eq(comparator_3_eq));  // open: gt, lt
  Comparator #(.width(3)) comparator_4 (.a(inst[14:12]), .b(3'b010), .eq(comparator_4_eq));  // open: gt, lt
  Comparator #(.width(3)) comparator_5 (.a(inst[14:12]), .b(3'b100), .eq(comparator_5_eq));  // open: gt, lt
  Comparator #(.width(3)) comparator_6 (.a(inst[14:12]), .b(3'b101), .eq(comparator_6_eq));  // open: gt, lt
  Comparator #(.width(3)) comparator_7 (.a(inst[14:12]), .b(3'b101), .eq(comparator_7_eq));  // open: gt, lt
  Comparator #(.width(3)) comparator_8 (.a(inst[14:12]), .b(3'b110), .eq(comparator_8_eq));  // open: gt, lt
  Comparator #(.width(3)) comparator_9 (.a(inst[14:12]), .b(3'b111), .eq(comparator_9_eq));  // open: gt, lt
  assign bit_extender_1_out = {{1{1'b0}}, priority_encoder_1_out};  // Bit_Extender bit_extender_1
  Priority_Encoder #(.select(5)) priority_encoder_1 (
    .in15(is_addi), .in16(is_slli), .in17(is_slti), .in18(is_xori), .in19(is_srli), .in20(is_srai),
    .in21(is_ori), .in22(is_andi), .out(priority_encoder_1_out));  // open: in0, in1, in2, in3, in4, in5, in6, in7, in8, in9, in10, in11, in12, in13, in14, in23, in24, in25, in26, in27, in28, in29, in30, in31, gs, en_out, en_in
  and and_1 (is_addi, is_i_type, comparator_2_eq);
  and and_2 (is_slli, is_i_type, comparator_3_eq);
  and and_3 (is_slti, is_i_type, comparator_4_eq);
  and and_4 (is_xori, is_i_type, comparator_5_eq);
  and and_5 (is_srli, is_i_type, comparator_6_eq);
  and and_6 (is_srai, is_i_type, comparator_7_eq);
  and and_7 (is_ori, is_i_type, comparator_8_eq);
  and and_8 (is_andi, is_i_type, comparator_9_eq);
  ROM #(.addrWidth(6), .dataWidth(16)) rom_1 (.addr(bit_extender_1_out), .data(rom_1_data));

  // Other names for the same wires on the sheet: opcode[6:0] = inst[6:0]; func3[2:0] = inst[14:12]

  // Notes on the sheet:
  //   INPUTS to your circuit
  //   Connect ROM Input here ->
  //   contents of rom_1 (hex, n*v repeats v):
  //   15*0 9204 9224 9244 9284 92a4 93a4 92c4 92e4
  //   ROM FOR CONTROL LOGIC
  //   DON'T CHANGE THE LOCATIONS OF THE INPUTS AND OUTPUTS!
  //   OUTPUT from your circuit
  //   CLOSE
  //   WIRE
  //   TO
  //   USE
  //   ROM
  //   Reminder: Use combinational logic for PCSel
endmodule
