// Logisim project cpu.circ as structural Verilog: 1 circuit, main circuit cpu
module cpu (
  input  clk,
  input  [31:0] INSTRUCTION,
  input  [31:0] MEM_READ_DATA,
  output [31:0] MEM_WRITE_ADDRESS,
  output [31:0] PROGRAM_COUNTER,
  output [31:0] ra,
  output [31:0] sp,
  output [31:0] t0,
  output [31:0] t1,
  output [31:0] t2,
  output [31:0] s0,
  output [31:0] s1,
  output [31:0] a0,
  output [31:0] tohost,
  output [3:0] MEM_WRITE_ENABLE,
  output [31:0] MEM_WRITE_DATA
);

  wire ASel, BrEq, BrLt, BrUn, BSel, CSRSel, CSRWen, PCSel, RegWEn;
  wire [1:0] WBSel;
  wire [2:0] control_logic_1_immsel;
  wire [3:0] ALUSel;
  wire [31:0] ALUResult, imm, multiplexer_1_out, multiplexer_2_out, multiplexer_3_out, PC4, pc4_t,
       Read_Data_1, Read_Data_2, WBSelOutput;

  Adder #(.width(32)) adder_1 (.a(PROGRAM_COUNTER), .b(32'h4), .out(pc4_t));  // open: cin, cout
  Register #(.width(32)) PC (.D(multiplexer_1_out), .clk(clk), .Q(PROGRAM_COUNTER));  // open: en, clr
  Multiplexer #(.enable("false"), .width(32)) multiplexer_1 (
    .in0(pc4_t), .in1(ALUResult), .out(multiplexer_1_out), .sel(PCSel));
  control_logic control_logic_1 (
    .CSRWen(CSRWen), .PCSel(PCSel), .RegWEn(RegWEn), .ImmSel(control_logic_1_immsel), .BrUn(BrUn),
    .BSel(BSel), .ALUSel(ALUSel), .WBSel(WBSel), .CSRSel(CSRSel), .inst(INSTRUCTION), .BrEq(BrEq), .BrLt(BrLt));  // open: ASel, MemRW
  imm_gen imm_gen_1 (.inst(INSTRUCTION), .ImmSel(control_logic_1_immsel), .imm(imm));
  regfile regfile_1 (
    .rs1(INSTRUCTION[19:15]), .rs2(INSTRUCTION[24:20]), .rd(INSTRUCTION[11:7]), .Write_Data(WBSelOutput),
    .RegWEn(RegWEn), .clk(clk), .ra(ra), .sp(sp), .t0(t0), .t1(t1), .t2(t2), .s0(s0), .s1(s1), .a0(a0),
    .Read_Data_1(Read_Data_1), .Read_Data_2(Read_Data_2));
  branch_comp branch_comp_1 (.rs1(Read_Data_1), .rs2(Read_Data_2), .BrUn(BrUn), .BrEq(BrEq), .BrLt(BrLt));
  Multiplexer #(.enable("false"), .width(32)) multiplexer_2 (
    .in0(Read_Data_1), .in1(PROGRAM_COUNTER), .out(multiplexer_2_out), .sel(ASel));
  Multiplexer #(.enable("false"), .width(32)) multiplexer_3 (
    .in0(Read_Data_2), .in1(imm), .out(multiplexer_3_out), .sel(BSel));
  alu alu_1 (.Result(ALUResult), .A(multiplexer_2_out), .B(multiplexer_3_out), .ALUSel(ALUSel));
  // csr csr_1: pin names not known; wires that end beside it: tohost
  Multiplexer #(.enable("false"), .select(2), .width(32)) multiplexer_4 (
    .in0(MEM_READ_DATA), .in1(ALUResult), .in2(PC4), .out(WBSelOutput), .sel(WBSel));  // open: in3

  // Other names for the same wires on the sheet: rd[4:0] = INSTRUCTION[11:7]; rs1[4:0] = INSTRUCTION[19:15];
  //   rs2[4:0] = INSTRUCTION[24:20]

  // Notes on the sheet:
  //   Output to IMEM
  //   IMEM (do **NOT** move this)
  //   Inputs from IMEM
  //   It is OK to move the PC, RegFile, ALU, MEM, Branch Comp, Imm Gen, and Control Logic to wherever is most convenient for you when constructing your CPU, and to delete this text
  //   Inputs/Outputs for testing. Do **NOT** move these.
  //   Outputs To DMEM
  //   DMEM (do **NOT** move this)
  //   Inputs From DMEM
endmodule
